// Logisim project Decodificador de 7 com Display.circ as structural Verilog: 1 circuit, main circuit main
module main (
  input  A,
  input  B,
  input  C,
  input  D,
  input  in_5,
  output out_6,
  output out_7,
  output out_8,
  output out_9,
  output out_10,
  output out_11,
  output out_12,
  output out_13,
  output out_14,
  output out_15
);

  wire _0_out, _1_out, _2_out, _3_out, _4_out, _5_out, _6_out, _7_out, _8_out, _9_out, A_out, B_out, C_out,
       D_out, E_out, F_out, G_out, not_1_out, not_2_out, not_3_out, not_4_out, not_5_out, not_6_out,
       not_7_out, not_8_out;

  not not_1 (not_1_out, A);
  not not_2 (not_2_out, not_1_out);
  not not_3 (not_3_out, B);
  not not_4 (not_4_out, not_3_out);
  not not_5 (not_5_out, C);
  not not_6 (not_6_out, not_5_out);
  not not_7 (not_7_out, D);
  not not_8 (not_8_out, not_7_out);
  nand _9 (_9_out, not_2_out, not_3_out, not_5_out, not_8_out);
  nand _8 (_8_out, not_2_out, not_3_out, not_5_out, not_7_out);
  nand _7 (_7_out, not_1_out, not_4_out, not_6_out, not_8_out);
  nand _6 (_6_out, not_1_out, not_4_out, not_6_out, not_7_out);
  nand _5 (_5_out, not_1_out, not_4_out, not_5_out, not_8_out);
  not not_9 (out_10, _5_out);
  not not_10 (out_11, _4_out);
  nand _4 (_4_out, not_1_out, not_4_out, not_5_out, not_7_out);
  nand _3 (_3_out, not_1_out, not_3_out, not_6_out, not_8_out);
  not not_11 (out_12, _3_out);
  not not_12 (out_13, _2_out);
  nand _2 (_2_out, not_1_out, not_3_out, not_6_out, not_7_out);
  nand _1 (_1_out, not_1_out, not_3_out, not_5_out, not_8_out);
  not not_13 (out_14, _1_out);
  nand _0 (_0_out, not_1_out, not_3_out, not_5_out, not_7_out);
  not not_14 (out_15, _0_out);
  not not_15 (out_6, _9_out);
  not not_16 (out_7, _8_out);
  not not_17 (out_8, _7_out);
  not not_18 (out_9, _6_out);
  or u_A (A_out, out_15, out_13, out_12, out_10, out_9, out_8, out_7, out_6);
  or u_B (B_out, out_15, out_14, out_13, out_12, out_11, out_8, out_7, out_6);
  or u_C (C_out, out_15, out_14, out_12, out_11, out_10, out_9, out_8, out_7, out_6);
  or u_D (D_out, out_15, out_13, out_12, out_10, out_9, out_7, out_6);
  _7_Segment_Display u_7_segment_display_1 (
    .g(G_out), .f(F_out), .a(A_out), .b(B_out), .e(E_out), .d(D_out), .c(C_out), .dp(in_5));
  or E (E_out, out_15, out_13, out_9, out_7);
  or F (F_out, out_15, out_11, out_10, out_9, out_7, out_6);
  or G (G_out, out_13, out_12, out_11, out_10, out_9, out_7, out_6);

  // Notes on the sheet:
  //   1001
  //   1000
  //   0111
  //   0110
  //   0101
  //   0100
  //   0011
  //   0010
  //   0001
  //   0000
endmodule
