// Logisim project Somador Subtrator Versão Final.circ as structural Verilog: 1 circuit, main circuit main
module main (
  input  A4,
  input  A3,
  input  A2,
  input  A1,
  input  A0,
  input  B4,
  input  B3,
  input  B2,
  input  B1,
  input  B0,
  input  SUBTRATOR,
  output SOMA,
  output CARRY_OUT,
  output SOMA_2,
  output CARRY_OUT_2,
  output SOMA_3,
  output CARRY_OUT_3,
  output SOMA_4,
  output CARRY_OUT_4,
  output MSB,
  output CARRY_OUT_5,
  output out_22,
  output out_23,
  output out_24,
  output out_25
);

  wire _0_2_out, _0_out, _1_2_out, _1_out, _2_2_out, _2_out, _3_2_out, _3_out, _4_2_out, _4_out, _5_2_out,
       _5_out, _6_2_out, _6_out, _7_out, _8_out, _9_out, _10_out, _11_out, _12_out, _13_out, _14_out,
       _15_out, A_2_out, A_out, and_1_out, and_2_out, and_3_out, and_4_out, and_5_out, and_6_out, and_7_out,
       and_8_out, and_9_out, and_10_out, and_11_out, and_12_out, and_13_out, and_14_out, and_15_out,
       and_16_out, B_2_out, B_out, C_2_out, C_out, D_2_out, D_out, E_2_out, E_out, F_2_out, F_out, G_2_out,
       G_out, minus_1_out, minus_2_out, minus_3_out, minus_4_out, minus_5_out, minus_6_out, minus_7_out,
       minus_8_out, minus_9_out, minus_10_out, minus_11_out, minus_12_out, minus_13_out, minus_14_out,
       minus_15_2_out, minus_15_out, not_1_out, not_2_out, not_3_out, not_4_out, not_5_out, not_6_out,
       not_7_out, not_8_out, not_9_out, not_10_out, not_11_out, not_12_out, not_13_out, not_14_out,
       not_15_out, not_16_out, not_17_out, not_18_out, not_19_out, not_20_out, not_21_out, not_22_out,
       not_23_out, not_24_out, not_25_out, not_26_out, not_27_out, not_28_out, not_29_out, not_30_out,
       not_31_out, not_32_out, not_33_out, not_34_out, not_35_out, not_36_out, not_37_out, not_38_out,
       not_39_out, not_40_out, not_41_out, not_42_out, not_43_out, not_44_out, not_45_out, not_46_out,
       not_47_out, not_48_out, not_49_out, not_50_out, not_51_out, not_52_out, not_53_out, not_54_out,
       not_55_out, or_1_out, or_2_out, or_3_out, or_4_out, or_5_out, or_6_out, or_7_out, or_8_out, or_9_out,
       or_10_out, OVERFLOW_out, xor_1_out, xor_2_out, xor_3_out, xor_4_out, xor_5_out, xor_6_out, xor_7_out,
       xor_8_out, xor_9_out, xor_10_out, xor_11_out, xor_22_out, xor_23_out, xor_24_out, xor_25_out,
       xor_26_out, xor_27_out, xor_28_out, xor_29_out, xor_30_out, xor_31_out, xor_32_out, xor_33_out,
       xor_34_out, xor_35_out, xor_36_out, xor_37_out;

  xor xor_1 (xor_1_out, B4, A4);
  xor xor_2 (xor_2_out, B0, SUBTRATOR);
  xor xor_3 (xor_3_out, B1, SUBTRATOR);
  xor xor_4 (xor_4_out, B2, SUBTRATOR);
  xor xor_5 (xor_5_out, B3, SUBTRATOR);
  xor xor_6 (xor_6_out, B4, SUBTRATOR);
  and and_1 (and_1_out, SUBTRATOR, ~B4, A4);  // AND_Gate
  xor xor_7 (xor_7_out, A0, xor_2_out);
  xor xor_8 (xor_8_out, A1, xor_3_out);
  xor xor_9 (xor_9_out, A2, xor_4_out);
  xor xor_10 (xor_10_out, A3, xor_5_out);
  xor xor_11 (xor_11_out, A4, xor_6_out);
  not not_1 (not_1_out, out_22);
  not not_2 (not_2_out, MSB);
  not not_3 (not_3_out, MSB);
  not not_4 (not_4_out, MSB);
  not not_5 (not_5_out, MSB);
  not not_6 (not_6_out, MSB);
  not not_7 (not_7_out, MSB);
  not not_8 (not_8_out, MSB);
  not not_9 (not_9_out, MSB);
  not not_10 (not_10_out, MSB);
  not not_11 (not_11_out, MSB);
  not not_12 (not_12_out, MSB);
  not not_13 (not_13_out, MSB);
  not not_14 (not_14_out, MSB);
  not not_15 (not_15_out, MSB);
  not not_16 (not_16_out, MSB);
  xor xor_12 (out_25, xor_7_out, SUBTRATOR);
  and and_2 (and_2_out, xor_7_out, SUBTRATOR);
  and and_3 (and_3_out, A0, xor_2_out);
  and and_4 (and_4_out, CARRY_OUT, xor_8_out);
  and and_5 (and_5_out, A1, xor_3_out);
  and and_6 (and_6_out, CARRY_OUT_2, xor_9_out);
  and and_7 (and_7_out, A2, xor_4_out);
  and and_8 (and_8_out, CARRY_OUT_3, xor_10_out);
  and and_9 (and_9_out, A3, xor_5_out);
  and and_10 (and_10_out, CARRY_OUT_4, xor_11_out);
  and and_11 (and_11_out, A4, xor_6_out);
  and and_12 (and_12_out, SUBTRATOR, xor_1_out);
  not not_17 (not_17_out, out_23);
  not not_18 (not_18_out, not_1_out);
  xor xor_13 (CARRY_OUT, and_2_out, and_3_out);
  xor xor_14 (out_24, xor_8_out, CARRY_OUT);
  xor xor_15 (CARRY_OUT_2, and_4_out, and_5_out);
  xor xor_16 (out_23, xor_9_out, CARRY_OUT_2);
  xor xor_17 (CARRY_OUT_3, and_6_out, and_7_out);
  xor xor_18 (out_22, xor_10_out, CARRY_OUT_3);
  xor xor_19 (CARRY_OUT_4, and_8_out, and_9_out);
  xor xor_20 (MSB, xor_11_out, CARRY_OUT_4);
  xor xor_21 (CARRY_OUT_5, and_10_out, and_11_out);
  not not_19 (not_19_out, out_24);
  not not_20 (not_20_out, not_17_out);
  not not_21 (not_21_out, out_25);
  not not_22 (not_22_out, not_19_out);
  not not_23 (not_23_out, not_21_out);
  nand _15 (_15_out, not_18_out, not_20_out, not_2_out, not_22_out, not_23_out);
  nand _14 (_14_out, not_18_out, not_20_out, not_3_out, not_22_out, not_21_out);
  nand _13 (_13_out, not_18_out, not_20_out, not_4_out, not_19_out, not_23_out);
  nand _12 (_12_out, not_18_out, not_20_out, not_5_out, not_19_out, not_21_out);
  nand _11 (_11_out, not_18_out, not_17_out, not_6_out, not_22_out, not_23_out);
  nand _10 (_10_out, not_18_out, not_17_out, not_7_out, not_22_out, not_21_out);
  nand _9 (_9_out, not_18_out, not_17_out, not_8_out, not_19_out, not_23_out);
  nand _8 (_8_out, not_18_out, not_17_out, not_9_out, not_19_out, not_21_out);
  nand _7 (_7_out, not_1_out, not_20_out, not_10_out, not_22_out, not_23_out);
  nand _6 (_6_out, not_1_out, not_20_out, not_11_out, not_22_out, not_21_out);
  nand _5 (_5_out, not_1_out, not_20_out, not_12_out, not_19_out, not_23_out);
  nand _4 (_4_out, not_1_out, not_20_out, not_13_out, not_19_out, not_21_out);
  nand _3 (_3_out, not_1_out, not_17_out, not_14_out, not_22_out, not_23_out);
  nand _2 (_2_out, not_1_out, not_17_out, not_15_out, not_22_out, not_21_out);
  nand _1 (_1_out, not_1_out, not_17_out, not_16_out, not_19_out, not_23_out);
  nand _0 (_0_out, not_1_out, not_17_out, ~MSB, not_19_out, not_21_out);  // NAND_Gate
  nand minus_1 (minus_1_out, not_23_out, not_22_out, MSB, not_20_out, not_18_out);
  nand minus_2 (minus_2_out, not_21_out, not_22_out, MSB, not_20_out, not_18_out);
  nand minus_3 (minus_3_out, not_23_out, not_19_out, MSB, not_20_out, not_18_out);
  nand minus_4 (minus_4_out, not_21_out, not_19_out, MSB, not_20_out, not_18_out);
  nand minus_5 (minus_5_out, not_23_out, not_22_out, MSB, not_17_out, not_18_out);
  nand minus_6 (minus_6_out, not_21_out, not_22_out, MSB, not_17_out, not_18_out);
  nand minus_7 (minus_7_out, not_23_out, not_19_out, MSB, not_17_out, not_18_out);
  nand minus_8 (minus_8_out, not_21_out, not_19_out, MSB, not_17_out, not_18_out);
  nand minus_9 (minus_9_out, not_23_out, not_22_out, MSB, not_20_out, not_1_out);
  nand minus_10 (minus_10_out, not_21_out, not_22_out, MSB, not_20_out, not_1_out);
  nand minus_11 (minus_11_out, not_23_out, not_19_out, MSB, not_20_out, not_1_out);
  nand minus_12 (minus_12_out, not_21_out, not_19_out, MSB, not_20_out, not_1_out);
  nand minus_13 (minus_13_out, not_23_out, not_22_out, MSB, not_17_out, not_1_out);
  nand minus_14 (minus_14_out, not_21_out, not_22_out, MSB, not_17_out, not_1_out);
  nand minus_15 (minus_15_out, not_23_out, not_19_out, MSB, not_17_out, not_1_out);
  nand minus_15_2 (minus_15_2_out, not_21_out, not_19_out, MSB, not_17_out, not_1_out);
  _7_Segment_Display u_7_segment_display_1 (.g(MSB));  // open: f, a, b, e, d, c, dp
  LED led_1 (.in(xor_22_out));
  xor OVERFLOW (OVERFLOW_out, CARRY_OUT_4, CARRY_OUT_5);
  not not_24 (not_24_out, _15_out);
  not not_25 (not_25_out, _14_out);
  not not_26 (not_26_out, _13_out);
  not not_27 (not_27_out, _12_out);
  not not_28 (not_28_out, _11_out);
  not not_29 (not_29_out, _10_out);
  not not_30 (not_30_out, _9_out);
  not not_31 (not_31_out, _8_out);
  not not_32 (not_32_out, _7_out);
  not not_33 (not_33_out, _6_out);
  not not_34 (not_34_out, _5_out);
  not not_35 (not_35_out, _4_out);
  not not_36 (not_36_out, _3_out);
  not not_37 (not_37_out, _2_out);
  not not_38 (not_38_out, _1_out);
  not not_39 (not_39_out, _0_out);
  not not_40 (not_40_out, minus_1_out);
  not not_41 (not_41_out, minus_2_out);
  not not_42 (not_42_out, minus_3_out);
  not not_43 (not_43_out, minus_4_out);
  not not_44 (not_44_out, minus_5_out);
  not not_45 (not_45_out, minus_6_out);
  not not_46 (not_46_out, minus_7_out);
  not not_47 (not_47_out, minus_8_out);
  not not_48 (not_48_out, minus_9_out);
  not not_49 (not_49_out, minus_10_out);
  not not_50 (not_50_out, minus_11_out);
  not not_51 (not_51_out, minus_12_out);
  not not_52 (not_52_out, minus_13_out);
  not not_53 (not_53_out, minus_14_out);
  not not_54 (not_54_out, minus_15_out);
  not not_55 (not_55_out, minus_15_2_out);
  _7_Segment_Display u_7_segment_display_2 (
    .g(and_13_out), .f(or_6_out), .a(or_1_out), .b(or_2_out), .e(or_5_out), .d(or_4_out), .c(or_3_out));  // open: dp
  _7_Segment_Display u_7_segment_display_3 (
    .g(or_10_out), .f(or_9_out), .a(or_7_out), .b(and_14_out), .e(or_8_out), .d(and_16_out), .c(and_15_out));  // open: dp
  ExactlyOne xor_22 (.out(xor_22_out), .in0(and_12_out), .in1(and_1_out), .in2(OVERFLOW_out));
  xor xor_23 (xor_23_out, not_24_out, not_54_out);
  xor xor_24 (xor_24_out, not_25_out, not_53_out);
  xor xor_25 (xor_25_out, not_26_out, not_52_out);
  xor xor_26 (xor_26_out, not_27_out, not_51_out);
  xor xor_27 (xor_27_out, not_28_out, not_50_out);
  xor xor_28 (xor_28_out, not_29_out, not_49_out);
  xor xor_29 (xor_29_out, not_30_out, not_48_out);
  xor xor_30 (xor_30_out, not_31_out, not_47_out);
  xor xor_31 (xor_31_out, not_32_out, not_46_out);
  xor xor_32 (xor_32_out, not_33_out, not_45_out);
  xor xor_33 (xor_33_out, not_34_out, not_44_out);
  xor xor_34 (xor_34_out, not_35_out, not_43_out);
  xor xor_35 (xor_35_out, not_36_out, not_42_out);
  xor xor_36 (xor_36_out, not_37_out, not_41_out);
  xor xor_37 (xor_37_out, not_38_out, not_40_out);
  or or_1 (or_1_out, xor_22_out, A_out);
  or A (A_out, xor_29_out, xor_30_out, xor_31_out, xor_32_out, xor_33_out, xor_34_out, xor_35_out, xor_36_out, xor_37_out, not_39_out);
  or or_2 (or_2_out, xor_22_out, B_out);
  or or_3 (or_3_out, xor_22_out, C_out);
  or B (B_out, xor_23_out, xor_24_out, xor_25_out, xor_26_out, xor_27_out, xor_28_out, xor_29_out, xor_30_out, not_55_out, xor_31_out, xor_32_out, xor_33_out, xor_34_out, xor_35_out, xor_36_out, xor_37_out, not_39_out);
  or or_4 (or_4_out, xor_22_out, D_out);
  or C (C_out, xor_23_out, xor_24_out, xor_25_out, xor_26_out, xor_27_out, xor_28_out, xor_29_out, xor_30_out, not_55_out, xor_31_out, xor_32_out, xor_33_out, xor_34_out, xor_35_out, xor_36_out, xor_37_out, not_39_out);
  or or_5 (or_5_out, xor_22_out, E_out);
  or D (D_out, xor_29_out, xor_30_out, xor_31_out, xor_32_out, xor_33_out, xor_34_out, xor_35_out, xor_36_out, xor_37_out, not_39_out);
  or E (E_out, xor_29_out, xor_30_out, xor_31_out, xor_32_out, xor_33_out, xor_34_out, xor_35_out, xor_36_out, xor_37_out, not_39_out);
  or or_6 (or_6_out, xor_22_out, F_out);
  or F (F_out, xor_29_out, xor_30_out, xor_31_out, xor_32_out, xor_33_out, xor_34_out, xor_35_out, xor_36_out, xor_37_out, not_39_out);
  and and_13 (and_13_out, ~xor_22_out, G_out);  // AND_Gate
  // OR_Gate G has open pins: out=G_out
  or _6_2 (_6_2_out, not_55_out, xor_32_out);
  or _5_2 (_5_2_out, xor_23_out, xor_33_out);
  or _4_2 (_4_2_out, xor_24_out, xor_34_out);
  or _3_2 (_3_2_out, xor_25_out, xor_35_out);
  or _2_2 (_2_2_out, xor_26_out, xor_36_out);
  or _1_2 (_1_2_out, xor_27_out, xor_37_out);
  or _0_2 (_0_2_out, xor_28_out, not_39_out);
  or or_7 (or_7_out, xor_22_out, A_2_out);
  or A_2 (A_2_out, _0_2_out, _2_2_out, _3_2_out, _5_2_out, _6_2_out, xor_31_out, xor_30_out, xor_29_out);
  and and_14 (and_14_out, ~xor_22_out, B_2_out);  // AND_Gate
  or B_2 (B_2_out, _0_2_out, _1_2_out, _2_2_out, _3_2_out, _4_2_out, xor_31_out, xor_30_out, xor_29_out);
  and and_15 (and_15_out, ~xor_22_out, C_2_out);  // AND_Gate
  or C_2 (C_2_out, _0_2_out, _1_2_out, _3_2_out, _4_2_out, _5_2_out, _6_2_out, xor_31_out, xor_30_out, xor_29_out);
  and and_16 (and_16_out, ~xor_22_out, D_2_out);  // AND_Gate
  or D_2 (D_2_out, _0_2_out, _2_2_out, _3_2_out, _5_2_out, _6_2_out, xor_30_out, xor_29_out);
  or or_8 (or_8_out, xor_22_out, E_2_out);
  or E_2 (E_2_out, _0_2_out, _2_2_out, _6_2_out, xor_30_out);
  or or_9 (or_9_out, xor_22_out, F_2_out);
  or F_2 (F_2_out, _0_2_out, _4_2_out, _5_2_out, _6_2_out, xor_30_out, xor_29_out);
  or or_10 (or_10_out, xor_22_out, G_2_out);
  or G_2 (G_2_out, _2_2_out, _3_2_out, _4_2_out, _5_2_out, _6_2_out, xor_30_out, xor_29_out);

  assign SOMA = out_25;
  assign SOMA_2 = out_24;
  assign SOMA_3 = out_23;
  assign SOMA_4 = out_22;

  // Notes on the sheet:
  //   NÚMERO A
  //   NÚMERO B
  //   1111
  //   1110
  //   1101
  //   1100
  //   1011
  //   1010
  //   1001
  //   1000
  //   0111
  //   0110
  //   0101
  //   0100
  //   0011
  //   0010
  //   0001
  //   0000
  //   11111
  //   11110
  //   11101
  //   11100
  //   11011
  //   11010
  //   11001
  //   11000
  //   10111
  //   10110
  //   10101
  //   10100
  //   10011
  //   10010
  //   10001
  //   10000
endmodule
