// Logisim project Somador-Subtrator 5bits by ERIC Vicente.circ as structural Verilog: 1 circuit, main circuit main
module main (
  input  BIT_DE_CONTROLE,
  input  A4,
  input  A3,
  input  A2,
  input  A1,
  input  A0,
  input  B4,
  input  B3,
  input  B2,
  input  B1,
  input  B0,
  input  in_12,
  output C0,
  output S0,
  output S1,
  output C1,
  output S2,
  output C2,
  output S3,
  output C3,
  output CarryOut,
  output S4_MSB,
  output out_23,
  output out_24,
  output out_25,
  output out_26,
  output out_27,
  output out_28,
  output out_29,
  output out_30,
  output out_31,
  output out_32
);

  wire _0_out, _1_out, _2_out, _3_out, _4_out, _5_out, _6_out, _7_out, _8_out, _9_out, _10_out, _11_out,
       _12_out, _13_out, _14_out, _15_out, A_out, and_1_out, and_2_out, and_3_out, and_4_out, and_5_out,
       and_6_out, and_7_out, and_8_out, and_9_out, and_10_out, and_11_out, and_12_out, and_13_out, B_out,
       C_out, D_out, E_out, F_out, G_out, minus_16_out, not_1_out, not_2_out, not_3_out, not_4_out,
       not_5_out, not_6_out, not_7_out, not_8_out, not_9_out, not_10_out, not_11_out, not_12_out, not_13_out,
       not_14_out, not_15_out, not_16_out, not_20_out, not_21_out, not_22_out, not_23_out, not_24_out,
       not_25_out, not_26_out, not_27_out, or_1_out, xor_2_out, xor_6_out, xor_9_out, xor_10_out, xor_13_out,
       xor_15_out, xor_17_out, xor_18_out, xor_19_out, xor_20_out, xor_21_out, xor_22_out, xor_23_out,
       xor_24_out, xor_25_out, xor_26_out, xor_27_out, xor_28_out, xor_29_out, xor_30_out;

  and and_1 (and_1_out, A4, xor_17_out);
  and and_2 (and_2_out, xor_2_out, C3);
  xor xor_1 (CarryOut, and_1_out, and_2_out);
  xor xor_2 (xor_2_out, A4, xor_17_out);
  xor xor_3 (S4_MSB, xor_2_out, C3);
  and and_3 (and_3_out, A3, xor_18_out);
  and and_4 (and_4_out, xor_6_out, C2);
  xor xor_4 (C3, and_3_out, and_4_out);
  xor xor_5 (S3, xor_6_out, C2);
  and and_5 (and_5_out, A2, xor_23_out);
  xor xor_6 (xor_6_out, A3, xor_18_out);
  and and_6 (and_6_out, xor_10_out, C1);
  xor xor_7 (C2, and_5_out, and_6_out);
  xor xor_8 (S2, xor_10_out, C1);
  xor xor_9 (xor_9_out, C3, CarryOut);
  xor xor_10 (xor_10_out, A2, xor_23_out);
  and and_7 (and_7_out, A1, xor_26_out);
  and and_8 (and_8_out, xor_13_out, C0);
  xor xor_11 (C1, and_7_out, and_8_out);
  xor xor_12 (S1, xor_13_out, C0);
  xor xor_13 (xor_13_out, A1, xor_26_out);
  and and_9 (and_9_out, A0, xor_25_out);
  xor xor_14 (C0, and_9_out, and_10_out);
  and and_10 (and_10_out, xor_15_out, BIT_DE_CONTROLE);
  xor xor_15 (xor_15_out, A0, xor_25_out);
  xor xor_16 (S0, xor_15_out, BIT_DE_CONTROLE);
  xor xor_17 (xor_17_out, B4, BIT_DE_CONTROLE);
  xor xor_18 (xor_18_out, B3, BIT_DE_CONTROLE);
  xor xor_19 (xor_19_out, S4_MSB, S0);
  and and_11 (and_11_out, xor_19_out, S4_MSB);
  xor xor_20 (xor_20_out, S1, S4_MSB);
  and and_12 (and_12_out, xor_20_out, and_11_out);
  xor xor_21 (xor_21_out, S4_MSB, S2);
  and and_13 (and_13_out, xor_21_out, and_12_out);
  xor xor_22 (xor_22_out, S3, S4_MSB);
  xor xor_23 (xor_23_out, B2, BIT_DE_CONTROLE);
  xor xor_24 (xor_24_out, xor_19_out, S4_MSB);
  xor xor_25 (xor_25_out, B0, BIT_DE_CONTROLE);
  xor xor_26 (xor_26_out, B1, BIT_DE_CONTROLE);
  xor xor_27 (xor_27_out, and_11_out, xor_20_out);
  xor xor_28 (xor_28_out, and_12_out, xor_21_out);
  xor xor_29 (xor_29_out, and_13_out, xor_22_out);
  not not_1 (not_1_out, S4_MSB);
  not not_2 (not_2_out, xor_29_out);
  not not_3 (not_3_out, xor_28_out);
  not not_4 (not_4_out, not_2_out);
  not not_5 (not_5_out, xor_27_out);
  not not_6 (not_6_out, not_3_out);
  not not_7 (not_7_out, xor_24_out);
  not not_8 (not_8_out, not_5_out);
  not not_9 (not_9_out, not_7_out);
  LED OVERFLOW (.in(xor_9_out));
  _7_Segment_Display u_7_segment_display_1 (.g(S4_MSB));  // open: f, a, b, e, d, c, dp
  nand minus_16 (minus_16_out, not_2_out, not_3_out, S4_MSB, not_5_out, not_7_out);
  nand _15 (_15_out, not_9_out, not_8_out, not_6_out, not_4_out);
  nand _14 (_14_out, not_7_out, not_8_out, not_6_out, not_4_out);
  nand _13 (_13_out, not_9_out, not_5_out, not_6_out, not_4_out);
  nand _12 (_12_out, not_7_out, not_5_out, not_6_out, not_4_out);
  nand _11 (_11_out, not_4_out, not_3_out, not_8_out, not_9_out);
  nand _10 (_10_out, not_7_out, not_8_out, not_3_out, not_4_out);
  nand _9 (_9_out, not_4_out, not_3_out, not_5_out, not_9_out);
  nand _8 (_8_out, not_4_out, not_3_out, not_5_out, not_7_out);
  nand _7 (_7_out, not_2_out, not_6_out, not_8_out, not_9_out);
  nand _6 (_6_out, not_2_out, not_6_out, not_8_out, not_7_out);
  nand _5 (_5_out, not_2_out, not_6_out, not_5_out, not_9_out);
  nand _4 (_4_out, not_2_out, not_6_out, not_5_out, not_7_out);
  nand _3 (_3_out, not_2_out, not_3_out, not_8_out, not_9_out);
  nand _2 (_2_out, not_2_out, not_3_out, not_8_out, not_7_out);
  nand _1 (_1_out, not_2_out, not_3_out, not_5_out, not_9_out);
  nand _0 (_0_out, not_2_out, not_3_out, not_1_out, not_5_out, not_7_out);
  _7_Segment_Display u_7_segment_display_2 (
    .f(not_27_out), .a(not_27_out), .b(xor_30_out), .e(not_27_out), .d(not_27_out), .c(xor_30_out));  // open: g, dp
  xor xor_30 (xor_30_out, or_1_out, not_27_out);
  or or_1 (or_1_out, not_11_out, not_12_out, not_13_out, not_10_out, not_14_out, not_15_out, not_16_out);
  not not_10 (not_10_out, minus_16_out);
  not not_11 (not_11_out, _15_out);
  not not_12 (not_12_out, _14_out);
  not not_13 (not_13_out, _13_out);
  not not_14 (not_14_out, _12_out);
  not not_15 (not_15_out, _11_out);
  not not_16 (not_16_out, _10_out);
  not not_17 (out_23, _9_out);
  not not_18 (out_24, _8_out);
  not not_19 (out_25, _7_out);
  not not_20 (not_20_out, _6_out);
  not not_21 (not_21_out, _5_out);
  not not_22 (not_22_out, _4_out);
  not not_23 (not_23_out, _3_out);
  not not_24 (not_24_out, _2_out);
  not not_25 (not_25_out, _1_out);
  not not_26 (not_26_out, _0_out);
  _7_Segment_Display u_7_segment_display_3 (
    .g(G_out), .f(F_out), .a(A_out), .b(B_out), .e(E_out), .d(D_out), .c(C_out), .dp(in_12));
  not not_27 (not_27_out, or_1_out);
  or or_2 (out_26, not_10_out, not_20_out);
  or or_3 (out_27, not_11_out, not_21_out);
  or or_4 (out_29, not_13_out, not_23_out);
  or or_5 (out_30, not_14_out, not_24_out);
  or or_6 (out_31, not_15_out, not_25_out);
  or or_7 (out_32, not_16_out, not_26_out);
  or A (A_out, out_32, out_30, out_29, out_27, out_26, out_25, out_24, out_23);
  or or_8 (out_28, not_12_out, not_22_out);
  or B (B_out, out_32, out_31, out_30, out_29, out_28, out_25, out_24, out_23);
  or C (C_out, out_32, out_31, out_29, out_28, out_27, out_26, out_25, out_24, out_23);
  or D (D_out, out_32, out_30, out_29, out_27, out_26, out_24, out_23);
  or E (E_out, out_32, out_30, out_26, out_24);
  or F (F_out, out_32, out_28, out_27, out_26, out_24, out_23);
  or G (G_out, out_30, out_29, out_28, out_27, out_26, out_24, out_23);

  // Notes on the sheet:
  //   SOMADOR-SUBTRATOR 4
  //   MSB
  //   BIT DE SINAL
  //   SOMADOR-SUBTRATOR 3
  //   SOMADOR-SUBTRATOR 2
  //   VERIFICA OVERFLOW
  //   SOMADOR-SUBTRATOR 1
  //   ENTRADA A
  //   SOMADOR-SUBTRATOR 0
  //   0 SOMA
  //   1 SUBTRAÇÃO
  //   ENTRADA B
  //   Sistema de complemento a dois para a saida
  //   DECODIFICADOR
  //   SINAL
  //   SAIDA DISPLAY
endmodule
