// Logisim project Somador.circ as structural Verilog: 1 circuit, main circuit main
module main (
  input  A0,
  input  B0,
  input  A1,
  input  B1,
  input  A2,
  input  B2,
  input  A3,
  input  B3,
  input  A4,
  input  B4,
  output Soma,
  output Carry_Out,
  output Soma_2,
  output Carry_Out_2,
  output Soma_3,
  output Carry_Out_3,
  output Soma_4,
  output Carry_Out_4,
  output Soma_5,
  output Carry_Out_5
);

  wire AND_2_out, AND_3_out, AND_4_out, AND_5_out, AND_6_out, AND_7_out, AND_8_out, AND_9_out, AND_10_out,
       AND_11_out, AND_12_out, AND_13_out, XOR_2_out, XOR_3_out, XOR_4_out, XOR_5_out;

  xor XOR (Soma, A0, B0);
  and AND (Carry_Out, A0, B0);
  xor XOR_2 (XOR_2_out, B1, Carry_Out);
  and AND_2 (AND_2_out, A1, Carry_Out);
  and AND_3 (AND_3_out, B1, Carry_Out);
  and AND_4 (AND_4_out, A1, B1);
  xor XOR_3 (XOR_3_out, B2, Carry_Out_2);
  and AND_5 (AND_5_out, A2, Carry_Out_2);
  and AND_6 (AND_6_out, B2, Carry_Out_2);
  and AND_7 (AND_7_out, A2, B2);
  xor XOR_4 (XOR_4_out, B3, Carry_Out_3);
  and AND_8 (AND_8_out, A3, Carry_Out_3);
  and AND_9 (AND_9_out, B3, Carry_Out_3);
  and AND_10 (AND_10_out, A3, B3);
  xor XOR_5 (XOR_5_out, B4, Carry_Out_4);
  xor XOR_6 (Soma_2, A1, XOR_2_out);
  or or_1 (Carry_Out_2, AND_2_out, AND_3_out, AND_4_out);
  xor XOR_7 (Soma_3, A2, XOR_3_out);
  or or_2 (Carry_Out_3, AND_5_out, AND_6_out, AND_7_out);
  xor XOR_8 (Soma_4, A3, XOR_4_out);
  or or_3 (Carry_Out_4, AND_8_out, AND_9_out, AND_10_out);
  xor XOR_9 (Soma_5, A4, XOR_5_out);
  and AND_11 (AND_11_out, A4, Carry_Out_4);
  and AND_12 (AND_12_out, B4, Carry_Out_4);
  and AND_13 (AND_13_out, A4, B4);
  or or_4 (Carry_Out_5, AND_11_out, AND_12_out, AND_13_out);
endmodule
